# Fritzing sketch MotionSensor (saved by Fritzing 0.9.2b)
breadboards: 1

parts:
  Part1 = Arduino Uno (Rev3)
  R1 = Resistor [tolerance=±5% resistance=220 package=THT]
  LED1 = LED - 5mm [color="Red (633nm)" package="5 mm [THT]"]
  PIR1 = PIR sensor

nets:
  N1: Part1.D13/SCK, R1.Pin_1
  GND: Part1.GND, PIR1.GND
  N2: Part1.D2, PIR1.SIG
  5V: Part1.5V, PIR1.VDD
  N3: R1.Pin_0, LED1.anode
